// Logisim project ALU.circ as structural Verilog: 5 circuits, main circuit ALU32Bit
module oneBitAdder (
  input  A,
  input  B,
  input  Cin,
  output S,
  output Cout
);

  wire and_1_out, and_2_out, xor_1_out;

  xor xor_1 (xor_1_out, A, B);
  xor xor_2 (S, xor_1_out, Cin);
  and and_1 (and_1_out, xor_1_out, Cin);
  and and_2 (and_2_out, A, B);
  or or_1 (Cout, and_1_out, and_2_out);
endmodule

module oneBitALU (
  input  [3:0] ALU_Ctrl,
  input  A,
  input  B,
  input  C_in,
  output R,
  output C_out
);

  wire and_1_out, multiplexer_1_out, not_1_out, onebitadder_1_s, or_1_out, xor_1_out;

  Multiplexer #(.enable("false")) multiplexer_1 (.in0(B), .in1(not_1_out), .out(multiplexer_1_out), .sel(ALU_Ctrl[2]));
  not not_1 (not_1_out, B);
  and and_1 (and_1_out, A, multiplexer_1_out);
  or or_1 (or_1_out, A, multiplexer_1_out);
  xor xor_1 (xor_1_out, A, multiplexer_1_out);
  oneBitAdder onebitadder_1 (.A(A), .B(multiplexer_1_out), .Cin(C_in), .S(onebitadder_1_s), .Cout(C_out));
  Multiplexer #(.enable("false"), .select(2)) multiplexer_2 (
    .in0(and_1_out), .in1(or_1_out), .in2(xor_1_out), .in3(onebitadder_1_s), .out(R), .sel(ALU_Ctrl[1:0]));
endmodule

module ALU4Bit (
  input  [3:0] ALU_Ctrl,
  input  [3:0] A,
  input  [3:0] B,
  input  C_in,
  output [3:0] R,
  output C_out
);

  wire onebitalu_1_c_out, onebitalu_2_c_out, onebitalu_3_c_out;

  oneBitALU onebitalu_1 (.ALU_Ctrl(ALU_Ctrl), .A(A[0]), .B(B[0]), .C_in(C_in), .R(R[0]), .C_out(onebitalu_1_c_out));
  oneBitALU onebitalu_2 (
    .ALU_Ctrl(ALU_Ctrl), .A(A[1]), .B(B[1]), .C_in(onebitalu_1_c_out), .R(R[1]), .C_out(onebitalu_2_c_out));
  oneBitALU onebitalu_3 (
    .ALU_Ctrl(ALU_Ctrl), .A(A[2]), .B(B[2]), .C_in(onebitalu_2_c_out), .R(R[2]), .C_out(onebitalu_3_c_out));
  oneBitALU onebitalu_4 (.ALU_Ctrl(ALU_Ctrl), .A(A[3]), .B(B[3]), .C_in(onebitalu_3_c_out), .R(R[3]), .C_out(C_out));
endmodule

module ALU32Bit (
  input  [3:0] ALU_Ctrl,
  input  [31:0] A,
  input  [31:0] B,
  output [31:0] R,
  output C_out
);

  wire alu4bit_1_c_out, alu4bit_2_c_out, alu4bit_3_c_out, alu4bit_4_c_out, alu4bit_5_c_out, alu4bit_6_c_out,
       alu4bit_7_c_out;

  ALU4Bit alu4bit_1 (
    .ALU_Ctrl(ALU_Ctrl), .A(A[3:0]), .B(B[3:0]), .C_in(ALU_Ctrl[2]), .R(R[3:0]), .C_out(alu4bit_1_c_out));
  ALU4Bit alu4bit_2 (
    .ALU_Ctrl(ALU_Ctrl), .A(A[7:4]), .B(B[7:4]), .C_in(alu4bit_1_c_out), .R(R[7:4]), .C_out(alu4bit_2_c_out));
  ALU4Bit alu4bit_3 (
    .ALU_Ctrl(ALU_Ctrl), .A(A[11:8]), .B(B[11:8]), .C_in(alu4bit_2_c_out), .R(R[11:8]),
    .C_out(alu4bit_3_c_out));
  ALU4Bit alu4bit_4 (
    .ALU_Ctrl(ALU_Ctrl), .A(A[15:12]), .B(B[15:12]), .C_in(alu4bit_3_c_out), .R(R[15:12]),
    .C_out(alu4bit_4_c_out));
  ALU4Bit alu4bit_5 (
    .ALU_Ctrl(ALU_Ctrl), .A(A[19:16]), .B(B[19:16]), .C_in(alu4bit_4_c_out), .R(R[19:16]),
    .C_out(alu4bit_5_c_out));
  ALU4Bit alu4bit_6 (
    .ALU_Ctrl(ALU_Ctrl), .A(A[23:20]), .B(B[23:20]), .C_in(alu4bit_5_c_out), .R(R[23:20]),
    .C_out(alu4bit_6_c_out));
  ALU4Bit alu4bit_7 (
    .ALU_Ctrl(ALU_Ctrl), .A(A[27:24]), .B(B[27:24]), .C_in(alu4bit_6_c_out), .R(R[27:24]),
    .C_out(alu4bit_7_c_out));
  ALU4Bit alu4bit_8 (
    .ALU_Ctrl(ALU_Ctrl), .A(A[31:28]), .B(B[31:28]), .C_in(alu4bit_7_c_out), .R(R[31:28]), .C_out(C_out));
endmodule

module ALUCtrl (
  input  i30,
  input  i14,
  input  i13,
  input  i12,
  input  i6,
  input  i5,
  input  i4,
  output ALU_CTRL3,
  output ALU_CTRL2,
  output ALU_CTRL1,
  output ALU_CTRL0,
  output ALU_SRC
);

  wire and_1_out, not_1_out, not_2_out, not_3_out, not_4_out, not_5_out;

  not not_1 (not_1_out, i14);
  not not_2 (not_2_out, i13);
  not not_3 (not_3_out, i12);
  not not_4 (not_4_out, i5);
  not not_5 (not_5_out, i4);
  or or_1 (ALU_CTRL1, not_2_out, not_5_out);
  and and_1 (and_1_out, i13, not_3_out);
  or or_2 (ALU_SRC, not_4_out, not_5_out);
  or or_3 (ALU_CTRL0, not_1_out, and_1_out);

  assign ALU_CTRL2 = i30;
  assign ALU_CTRL3 = 1'b0;
endmodule
