// Logisim project lab3.circ as structural Verilog: 2 circuits, main circuit processor
module processor (
  input  [31:0] Instruction,
  output [31:0] out_2
);

  wire alu32bit_1_c_out, alu_ctrl_1_alusrc, clock_1_out;
  wire [3:0] alu_ctrl_1_aluctrl0;
  wire [31:0] bit_extender_1_out, multiplexer_1_out, register_file_1_rdata1, register_file_1_rdata2;

  Clock clock_1 (.out(clock_1_out));
  assign bit_extender_1_out = {{20{Instruction[31]}}, Instruction[31:20]};  // Bit_Extender bit_extender_1
  register_file register_file_1 (
    .RReg1(Instruction[19:15]), .WData(out_2), .Clock_in(clock_1_out), .Write(1'b1),
    .WReg(Instruction[11:7]), .RReg2(Instruction[24:20]), .RData1(register_file_1_rdata1),
    .RData2(register_file_1_rdata2));
  ALU_Ctrl alu_ctrl_1 (
    .I30(Instruction[30]), .I14(Instruction[14]), .I13(Instruction[13]), .I12(Instruction[12]),
    .I6(Instruction[6]), .I5(Instruction[5]), .I4(Instruction[4]), .ALUCTRL3(alu_ctrl_1_aluctrl0[3]),
    .ALUCTRL2(alu_ctrl_1_aluctrl0[2]), .ALUCTRL1(alu_ctrl_1_aluctrl0[1]), .ALUCTRL0(alu_ctrl_1_aluctrl0[0]),
    .ALUSRC(alu_ctrl_1_alusrc));
  Multiplexer #(.enable("false"), .width(32)) multiplexer_1 (
    .in0(register_file_1_rdata2), .in1(bit_extender_1_out), .out(multiplexer_1_out), .sel(alu_ctrl_1_alusrc));
  ALU32Bit alu32bit_1 (
    .ALU_Ctrl(alu_ctrl_1_aluctrl0), .A(register_file_1_rdata1), .B(multiplexer_1_out), .R(out_2),
    .C_out(alu32bit_1_c_out));
endmodule

module ALU_Ctrl (
  input  I30,
  input  I14,
  input  I13,
  input  I12,
  input  I6,
  input  I5,
  input  I4,
  output ALUCTRL3,
  output ALUCTRL2,
  output ALUCTRL1,
  output ALUCTRL0,
  output ALUSRC
);

  wire and_2_out, not_1_out, not_2_out, not_3_out, not_4_out, not_5_out;

  not not_1 (not_1_out, I14);
  not not_2 (not_2_out, I13);
  not not_3 (not_3_out, I12);
  not not_4 (not_4_out, I5);
  not not_5 (not_5_out, I4);
  and and_1 (ALUCTRL2, I30, not_2_out, I5);
  or or_1 (ALUCTRL1, not_2_out, not_5_out);
  and and_2 (and_2_out, I13, not_3_out);
  or or_2 (ALUSRC, not_4_out, not_5_out);
  or or_3 (ALUCTRL0, not_1_out, and_2_out);

  assign ALUCTRL3 = 1'b0;
endmodule
